// Logisim project ex5.circ as structural Verilog: 9 circuits, main circuit rotr
module rotr (
  input  [15:0] A,
  input  [3:0] B,
  output [15:0] Out1
);

  wire [15:0] chooseonrot2_1_out_3, chooseonrot4_1_out_3, chooseonrot8_1_out_3;

  ChooseOnRot8 chooseonrot8_1 (.in_1(A), .in_2(B[3]), .out_3(chooseonrot8_1_out_3));
  ChooseOnRot2 chooseonrot2_1 (.in_1(chooseonrot4_1_out_3), .in_2(B[1]), .out_3(chooseonrot2_1_out_3));
  ChooseOnRot4 chooseonrot4_1 (.in_1(chooseonrot8_1_out_3), .in_2(B[2]), .out_3(chooseonrot4_1_out_3));
  ChooseOnRot1 chooseonrot1_1 (.in_1(chooseonrot2_1_out_3), .in_2(B[0]), .out_3(Out1));

  // Other names for the same wires on the sheet: Rot1Sel = B[0]; Rot2Sel = B[1]; Rot4Sel = B[2]; Rot8Sel = B[3];
  //   SysInput[15:0] = A

  // Notes on the sheet:
  //   PUT CIRCUITRY HERE
endmodule

module rot8 (
  input  [15:0] in_1,
  output [15:0] out_2
);


  assign out_2 = {in_1[7:0], in_1[15:8]};

  // Notes on the sheet:
  //   PUT CIRCUITRY HERE
endmodule

module rot4 (
  input  [15:0] in_1,
  output [15:0] out_2
);


  assign out_2 = {in_1[3:0], in_1[15:4]};

  // Notes on the sheet:
  //   PUT CIRCUITRY HERE
endmodule

module rot2 (
  input  [15:0] in_1,
  output [15:0] out_2
);


  assign out_2 = {in_1[1:0], in_1[15:2]};

  // Notes on the sheet:
  //   PUT CIRCUITRY HERE
endmodule

module rot1 (
  input  [15:0] in_1,
  output [15:0] out_2
);


  assign out_2 = {in_1[0], in_1[15:1]};

  // Notes on the sheet:
  //   PUT CIRCUITRY HERE
endmodule

module ChooseOnRot8 (
  input  [15:0] in_1,
  input  in_2,
  output [15:0] out_3
);

  wire [15:0] rot8_1_out_2;

  rot8 rot8_1 (.in_1(in_1), .out_2(rot8_1_out_2));
  Multiplexer #(.enable("false"), .width(16)) multiplexer_1 (.in0(in_1), .in1(rot8_1_out_2), .out(out_3), .sel(in_2));
endmodule

module ChooseOnRot4 (
  input  [15:0] in_1,
  input  in_2,
  output [15:0] out_3
);

  wire [15:0] rot4_1_out_2;

  rot4 rot4_1 (.in_1(in_1), .out_2(rot4_1_out_2));
  Multiplexer #(.enable("false"), .width(16)) multiplexer_1 (.in0(in_1), .in1(rot4_1_out_2), .out(out_3), .sel(in_2));
endmodule

module ChooseOnRot2 (
  input  [15:0] in_1,
  input  in_2,
  output [15:0] out_3
);

  wire [15:0] rot2_1_out_2;

  rot2 rot2_1 (.in_1(in_1), .out_2(rot2_1_out_2));
  Multiplexer #(.enable("false"), .width(16)) multiplexer_1 (.in0(in_1), .in1(rot2_1_out_2), .out(out_3), .sel(in_2));
endmodule

module ChooseOnRot1 (
  input  [15:0] in_1,
  input  in_2,
  output [15:0] out_3
);

  wire [15:0] rot1_1_out_2;

  rot1 rot1_1 (.in_1(in_1), .out_2(rot1_1_out_2));
  Multiplexer #(.enable("false"), .width(16)) multiplexer_1 (.in0(in_1), .in1(rot1_1_out_2), .out(out_3), .sel(in_2));
endmodule
