// Logisim project alu.circ as structural Verilog: 2 circuits, main circuit alu
module alu (
  input  [31:0] A,
  input  [31:0] B,
  input  [3:0] ALUSel,
  output [31:0] Result
);

  wire comparator_1_lt;
  wire [31:0] add0, and0, bsel, mul0, mulh, mulh0, mulhu, mulhu0, or0, sll0, slt0, sra0, srl0, sub0, xor0;

  Adder #(.width(32)) adder_1 (.a(A), .b(B), .out(add0));  // open: cin, cout
  assign and0 = A & B;  // AND_Gate and_1, 32 bits wide
  assign or0 = A | B;  // OR_Gate or_1, 32 bits wide
  assign xor0 = A ^ B;  // XOR_Gate xor_1, 32 bits wide
  Shifter #(.shift("lr"), .width(32)) shifter_1 (.in(A), .\dist (B[4:0]), .out(srl0));
  Shifter #(.shift("ar"), .width(32)) shifter_2 (.in(A), .\dist (B[4:0]), .out(sra0));
  Shifter #(.width(32)) shifter_3 (.in(A), .\dist (B[4:0]), .out(sll0));
  Multiplier #(.mode("twosComplement"), .width(32)) multiplier_1 (.a(A), .b(B), .out(mul0), .cout(mulh0));  // open: cin
  Subtractor #(.width(32)) subtractor_1 (.a(A), .b(B), .out(sub0));  // open: bin, bout
  Multiplier #(.width(32)) multiplier_2 (.a(A), .b(B), .cout(mulhu0));  // open: out, cin
  Comparator #(.width(32)) comparator_1 (.a(A), .b(B), .lt(comparator_1_lt));  // open: gt, eq
  ALU_Selector alu_selector_1 (
    .ALU_IN_0(add0), .ALU_IN_1(and0), .ALU_IN_2(or0), .ALU_IN_3(xor0), .ALU_IN_4(srl0), .ALU_IN_5(sra0),
    .ALU_IN_6(sll0), .ALU_IN_7(slt0), .ALU_IN_10(mul0), .ALU_IN_11(mulhu), .ALU_IN_12(sub0),
    .ALU_IN_13(bsel), .ALU_IN_14(mulh), .ALUSel(ALUSel), .out_15(Result));
  assign slt0 = {{31{1'b0}}, comparator_1_lt};  // Bit_Extender bit_extender_1

  // Other names for the same wires on the sheet: bsel0[31:0] = B

  // Notes on the sheet:
  //   INPUTS to your circuit
  //   DON'T CHANGE THE LOCATIONS OF THE INPUTS AND OUTPUTS!
  //   OUTPUT from your circuit
endmodule

module ALU_Selector (
  input  [31:0] ALU_IN_0,
  input  [31:0] ALU_IN_1,
  input  [31:0] ALU_IN_2,
  input  [31:0] ALU_IN_3,
  input  [31:0] ALU_IN_4,
  input  [31:0] ALU_IN_5,
  input  [31:0] ALU_IN_6,
  input  [31:0] ALU_IN_7,
  input  [31:0] ALU_IN_10,
  input  [31:0] ALU_IN_11,
  input  [31:0] ALU_IN_12,
  input  [31:0] ALU_IN_13,
  input  [31:0] ALU_IN_14,
  input  [3:0] ALUSel,
  output [31:0] out_15
);

  Multiplexer #(.enable("false"), .select(4), .width(32)) multiplexer_1 (
    .in0(ALU_IN_0), .in1(ALU_IN_1), .in2(ALU_IN_2), .in3(ALU_IN_3), .in4(ALU_IN_4), .in5(ALU_IN_5),
    .in6(ALU_IN_6), .in7(ALU_IN_7), .in8({32{1'b0}}), .in9({32{1'b0}}), .in10(ALU_IN_10), .in11(ALU_IN_11),
    .in12(ALU_IN_12), .in13(ALU_IN_13), .in14(ALU_IN_14), .in15({32{1'b0}}), .out(out_15), .sel(ALUSel));
endmodule
