// Logisim project branch_comp.circ as structural Verilog: 1 circuit, main circuit branch_comp
module branch_comp (
  input  [31:0] rs1,
  input  [31:0] rs2,
  input  BrUn,
  output BrEq,
  output BrLt
);

  wire Lt, ULt;

  Comparator #(.mode("unsigned"), .width(32)) comparator_1 (.a(rs1), .b(rs2), .eq(BrEq), .lt(ULt));  // open: gt
  Multiplexer #(.enable("false")) multiplexer_1 (.in0(Lt), .in1(ULt), .out(BrLt), .sel(BrUn));
  Comparator #(.width(32)) comparator_2 (.a(rs1), .b(rs2), .lt(Lt));  // open: gt, eq

  // Notes on the sheet:
  //   INPUTS to your circuit
  //   DON'T CHANGE THE LOCATIONS OF THE INPUTS AND OUTPUTS!
  //   OUTPUT from your circuit
endmodule
