// Logisim project control_logic.circ as structural Verilog: 2 circuits, main circuit control_logic
module control_logic (
  input  [31:0] inst,
  input  BrEq,
  input  BrLt,
  output PCSel,
  output RegWEn,
  output [2:0] ImmSel,
  output BrUn,
  output ASel,
  output BSel,
  output [3:0] ALUSel,
  output [3:0] MemRW,
  output [1:0] WBSel,
  output CSRSel,
  output CSRWen
);

  ROM #(.addrWidth(12), .dataWidth(20)) rom_1 (
    .addr({inst[6:2], inst[14:12], inst[30], inst[25], BrEq, BrLt}),
    .data({PCSel, RegWEn, ImmSel, BrUn, ASel, BSel, ALUSel, MemRW, WBSel, CSRSel, CSRWen}));

  // Other names for the same wires on the sheet: MulSel = inst[25]; SignBit = inst[30]; Funct3[2:0] = inst[14:12];
  //   Opcode_2_6[4:0] = inst[6:2]

  // Notes on the sheet:
  //   INPUTS to your circuit
  //   DON'T CHANGE THE LOCATIONS OF THE INPUTS AND OUTPUTS!
  //   OUTPUT from your circuit
  //   contents of rom_1 (hex, n*v repeats v):
  //   48*49000 464*0 16*49004 16*49604 16*49704 16*0 16*49304 8*49404 8*49504 16*49204 16*49104 128*63004
  //   256*0 16*11010 16*11030 16*110f0 464*0 4*40004 4*40a04 4*40c04 4*0 4*40604 4*40e04 8*0 4*40704 16*0
  //   4*40b04 8*0 4*40304 12*0 4*40404 4*0 4*40504 4*0 4*40204 12*0 4*40104 12*0 128*63d04 1280*0 1b000
  //   1b000 9b000 0 1b000 1b000 9b000 0 1b000 1b000 9b000 0 1b000 1b000 9b000 0 9b000 9b000 1b000 0 9b000
  //   9b000 1b000 0 9b000 9b000 1b000 0 9b000 9b000 1b000 33*0 1b000 9b000 1b000 0 1b000 9b000 1b000 0
  //   1b000 9b000 1b000 0 1b000 9b000 1b000 0 9b000 1b000 9b000 0 9b000 1b000 9b000 0 9b000 1b000 9b000 0
  //   9b000 1b000 9b000 0 1f000 9f000 1f000 0 1f000 9f000 1f000 0 1f000 9f000 1f000 0 1f000 9f000 1f000 0
  //   9f000 1f000 9f000 0 9f000 1f000 9f000 0 9f000 1f000 9f000 0 9f000 1f000 9f000 0 16*c9008 240*0
  //   128*eb008 16*0 16*8001 48*0 16*8003
endmodule

module ALU_Decode (
  input  [2:0] funct3,
  input  mul_Sel,
  input  SignBit,
  output [3:0] ALUSel
);

  wire [3:0] addOrSubOrMul, sllOrMulh, sltuOrMulhu, sra_l_0;

  Multiplexer #(.enable("false"), .width(4)) multiplexer_1 (.in0(4'b0100), .in1(4'b0101), .out(sra_l_0), .sel(SignBit));
  Multiplexer #(.enable("false"), .select(3), .width(4)) multiplexer_2 (
    .in0(addOrSubOrMul), .in1(sllOrMulh), .in2(4'b0111), .in3(sltuOrMulhu), .in4(4'b0011), .in5(sra_l_0),
    .in6(4'b0010), .in7(4'b0001), .out(ALUSel), .sel(funct3));
  Multiplexer #(.enable("false"), .select(2), .width(4)) multiplexer_3 (
    .in0(4'b0000), .in1(4'b1010), .in2(4'b1100), .out(addOrSubOrMul), .sel({SignBit, mul_Sel}));  // open: in3
  Multiplexer #(.enable("false"), .width(4)) multiplexer_4 (
    .in0(4'b0110), .in1(4'b1110), .out(sllOrMulh), .sel(mul_Sel));
  Multiplexer #(.enable("false"), .width(4)) multiplexer_5 (
    .in0(4'b0111), .in1(4'b1011), .out(sltuOrMulhu), .sel(mul_Sel));

  // Other names for the same wires on the sheet: MS = mul_Sel; S = SignBit
endmodule
