// Logisim project cpu.circ as structural Verilog: 1 circuit, main circuit cpu
module cpu (
  input  clk,
  input  [31:0] INSTRUCTION,
  input  [31:0] READ_DATA,
  output [31:0] WRITE_ADDRESS,
  output [31:0] PROGRAM_COUNTER,
  output [31:0] ra,
  output [31:0] sp,
  output [31:0] t0,
  output [31:0] t1,
  output [31:0] t2,
  output [31:0] s0,
  output [31:0] s1,
  output [31:0] a0,
  output [31:0] tohost,
  output [3:0] WRITE_ENABLE,
  output [31:0] WRITE_DATA
);

  wire ASel, BrEq, BrLt, BrUn, BSel, CSRSel, CSRWEn, PCSel, RegWEn;
  wire [1:0] WBSel;
  wire [2:0] ImmSel;
  wire [3:0] ALUSel;
  wire [31:0] adder_1_out, adder_2_out, Immediate, multiplexer_1_out, multiplexer_2_out, multiplexer_3_out,
       multiplexer_4_out, multiplexer_5_out, Reg_Ins, Reg_PC, rs1_Value, UImm, WriteBack;

  Adder #(.width(32)) adder_1 (.a(PROGRAM_COUNTER), .b(32'h4), .out(adder_1_out));  // open: cin, cout
  Multiplexer #(.enable("false"), .width(32)) multiplexer_1 (
    .in0(INSTRUCTION), .in1(32'h13), .out(multiplexer_1_out), .sel(PCSel));
  Register #(.width(32)) PC (.D(multiplexer_2_out), .clk(clk), .Q(PROGRAM_COUNTER));  // open: en, clr
  Multiplexer #(.enable("false"), .width(32)) multiplexer_2 (
    .in0(adder_1_out), .in1(WRITE_ADDRESS), .out(multiplexer_2_out), .sel(PCSel));
  Register #(.width(32)) register_1 (.D(multiplexer_1_out), .clk(clk), .Q(Reg_Ins));  // open: en, clr
  Register #(.width(32)) register_2 (.D(PROGRAM_COUNTER), .clk(clk), .Q(Reg_PC));  // open: en, clr
  control_logic control_logic_1 (
    .CSRWen(CSRWEn), .PCSel(PCSel), .RegWEn(RegWEn), .ImmSel(ImmSel), .BrUn(BrUn), .ASel(ASel), .BSel(BSel),
    .ALUSel(ALUSel), .MemRW(WRITE_ENABLE), .WBSel(WBSel), .CSRSel(CSRSel), .inst(Reg_Ins), .BrEq(BrEq),
    .BrLt(BrLt));
  assign UImm = {{27{1'b0}}, Reg_Ins[19:15]};  // Bit_Extender bit_extender_1
  imm_gen imm_gen_1 (.inst(Reg_Ins), .ImmSel(ImmSel), .imm(Immediate));
  regfile regfile_1 (
    .rs1(Reg_Ins[19:15]), .rs2(Reg_Ins[24:20]), .rd(Reg_Ins[11:7]), .Write_Data(WriteBack), .RegWEn(RegWEn),
    .clk(clk), .ra(ra), .sp(sp), .t0(t0), .t1(t1), .t2(t2), .s0(s0), .s1(s1), .a0(a0),
    .Read_Data_1(rs1_Value), .Read_Data_2(WRITE_DATA));
  branch_comp branch_comp_1 (.rs1(rs1_Value), .rs2(WRITE_DATA), .BrUn(BrUn), .BrEq(BrEq), .BrLt(BrLt));
  Multiplexer #(.enable("false"), .width(32)) multiplexer_3 (
    .in0(rs1_Value), .in1(Reg_PC), .out(multiplexer_3_out), .sel(ASel));
  Multiplexer #(.enable("false"), .width(32)) multiplexer_4 (
    .in0(WRITE_DATA), .in1(Immediate), .out(multiplexer_4_out), .sel(BSel));
  alu alu_1 (.Result(WRITE_ADDRESS), .A(multiplexer_3_out), .B(multiplexer_4_out), .ALUSel(ALUSel));
  Multiplexer #(.enable("false"), .width(32)) multiplexer_5 (
    .in0(rs1_Value), .in1(UImm), .out(multiplexer_5_out), .sel(CSRSel));
  csr csr_1 (.CSR_address({12{1'b0}}), .CSR_din(multiplexer_5_out), .CSR_WE(CSRWEn), .clk(clk), .tohost(tohost));
  Adder #(.width(32)) adder_2 (.a(Reg_PC), .b(32'h4), .out(adder_2_out));  // open: cin, cout
  Multiplexer #(.enable("false"), .select(2), .width(32)) multiplexer_6 (
    .in0(READ_DATA), .in1(WRITE_ADDRESS), .in2(adder_2_out), .out(WriteBack), .sel(WBSel));  // open: in3

  // Other names for the same wires on the sheet: ALUOutput[31:0] = WRITE_ADDRESS; rs2_Value[31:0] = WRITE_DATA

  // Notes on the sheet:
  //   Output to IMEM
  //   If branch taken, kill the next instruction that's going to be written to the InstReg
  //   IMEM (do **NOT** move this)
  //   Inputs from IMEM
  //   It is OK to move the PC, RegFile, ALU, MEM, Branch Comp, Imm Gen, and Control Logic to wherever is most convenient for you when constructing your CPU, and to delete this text
  //   Inputs/Outputs for testing. Do **NOT** move these.
  //   Outputs To DMEM
  //   DMEM (do **NOT** move this)
  //   Inputs From DMEM
endmodule
