// Logisim project regfile.circ as structural Verilog: 3 circuits, main circuit regfile
module regfile (
  input  [4:0] rs1,
  input  [4:0] rs2,
  input  [4:0] rd,
  input  [31:0] Write_Data,
  input  RegWEn,
  input  clk,
  output [31:0] ra,
  output [31:0] sp,
  output [31:0] t0,
  output [31:0] t1,
  output [31:0] t2,
  output [31:0] s0,
  output [31:0] s1,
  output [31:0] a0,
  output [31:0] Read_Data_1,
  output [31:0] out_16,
  output [31:0] Read_Data_2
);

  RegProcess regprocess_1 (
    .WriteData(Write_Data), .clk(clk), .WriteEnable(RegWEn), .rs1(rs1), .rs2(rs2), .rd(rd),
    .rs1_Output(Read_Data_1), .rs2_Output(Read_Data_2), .x0_output(out_16), .ra_output(ra), .sp_output(sp),
    .t0_output(t0), .t1_output(t1), .t2_output(t2), .s0_output(s0), .s1_output(s1), .a0_output(a0));

  // Other names for the same wires on the sheet: read_data1[31:0] = Read_Data_1; read_data2[31:0] = Read_Data_2;
  //   read_reg1[4:0] = rs1; read_reg2[4:0] = rs2; write_en = RegWEn; write_reg[4:0] = rd

  // Notes on the sheet:
  //   INPUTS to your circuit
  //   DON'T CHANGE THE LOCATIONS OF THE INPUTS AND OUTPUTS!
  //   These are DEBUG/TEST outputs from your circuit.
  //   OUTPUTS from your circuit
endmodule

module AllRegs (
  input  [31:0] WriteData,
  input  Clk,
  input  WEn0,
  input  WEn1,
  input  WEn2,
  input  WEn3,
  input  WEn4,
  input  WEn5,
  input  WEn6,
  input  WEn7,
  input  WEn8,
  input  WEn9,
  input  WEn10,
  input  WEn11,
  input  WEn12,
  input  WEn13,
  input  WEn14,
  input  WEn15,
  input  WEn16,
  input  WEn17,
  input  WEn18,
  input  WEn19,
  input  WEn20,
  input  WEn21,
  input  WEn22,
  input  WEn23,
  input  WEn24,
  input  WEn25,
  input  WEn26,
  input  WEn27,
  input  WEn28,
  input  WEn29,
  input  WEn30,
  input  WEn31,
  output [31:0] ReadData0,
  output [31:0] ReadData1,
  output [31:0] ReadData2,
  output [31:0] ReadData3,
  output [31:0] ReadData4,
  output [31:0] ReadData5,
  output [31:0] ReadData6,
  output [31:0] ReadData7,
  output [31:0] ReadData8,
  output [31:0] ReadData9,
  output [31:0] ReadData10,
  output [31:0] ReadData11,
  output [31:0] ReadData12,
  output [31:0] ReadData13,
  output [31:0] ReadData14,
  output [31:0] ReadData15,
  output [31:0] ReadData16,
  output [31:0] ReadData17,
  output [31:0] ReadData18,
  output [31:0] ReadData19,
  output [31:0] ReadData20,
  output [31:0] ReadData21,
  output [31:0] ReadData22,
  output [31:0] ReadData23,
  output [31:0] ReadData24,
  output [31:0] ReadData25,
  output [31:0] ReadData26,
  output [31:0] ReadData27,
  output [31:0] ReadData28,
  output [31:0] ReadData29,
  output [31:0] ReadData30,
  output [31:0] ReadData31
);

  Register #(.width(32)) x0 (.D(WriteData), .en(1'b0), .clk(Clk), .Q(ReadData0), .clr(1'b1));
  Register #(.width(32)) register_1 (.D(WriteData), .en(WEn8), .clk(Clk), .Q(ReadData8));  // open: clr
  Register #(.width(32)) register_2 (.D(WriteData), .en(WEn16), .clk(Clk), .Q(ReadData16));  // open: clr
  Register #(.width(32)) register_3 (.D(WriteData), .en(WEn24), .clk(Clk), .Q(ReadData24));  // open: clr
  Register #(.width(32)) x1 (.D(WriteData), .en(WEn1), .clk(Clk), .Q(ReadData1));  // open: clr
  Register #(.width(32)) register_4 (.D(WriteData), .en(WEn9), .clk(Clk), .Q(ReadData9));  // open: clr
  Register #(.width(32)) register_5 (.D(WriteData), .en(WEn17), .clk(Clk), .Q(ReadData17));  // open: clr
  Register #(.width(32)) register_6 (.D(WriteData), .en(WEn25), .clk(Clk), .Q(ReadData25));  // open: clr
  Register #(.width(32)) x2 (.D(WriteData), .en(WEn2), .clk(Clk), .Q(ReadData2));  // open: clr
  Register #(.width(32)) register_7 (.D(WriteData), .en(WEn10), .clk(Clk), .Q(ReadData10));  // open: clr
  Register #(.width(32)) register_8 (.D(WriteData), .en(WEn18), .clk(Clk), .Q(ReadData18));  // open: clr
  Register #(.width(32)) register_9 (.D(WriteData), .en(WEn26), .clk(Clk), .Q(ReadData26));  // open: clr
  Register #(.width(32)) register_10 (.D(WriteData), .en(WEn3), .clk(Clk), .Q(ReadData3));  // open: clr
  Register #(.width(32)) register_11 (.D(WriteData), .en(WEn11), .clk(Clk), .Q(ReadData11));  // open: clr
  Register #(.width(32)) register_12 (.D(WriteData), .en(WEn19), .clk(Clk), .Q(ReadData19));  // open: clr
  Register #(.width(32)) register_13 (.D(WriteData), .en(WEn27), .clk(Clk), .Q(ReadData27));  // open: clr
  Register #(.width(32)) register_14 (.D(WriteData), .en(WEn4), .clk(Clk), .Q(ReadData4));  // open: clr
  Register #(.width(32)) register_15 (.D(WriteData), .en(WEn12), .clk(Clk), .Q(ReadData12));  // open: clr
  Register #(.width(32)) register_16 (.D(WriteData), .en(WEn20), .clk(Clk), .Q(ReadData20));  // open: clr
  Register #(.width(32)) register_17 (.D(WriteData), .en(WEn28), .clk(Clk), .Q(ReadData28));  // open: clr
  Register #(.width(32)) register_18 (.D(WriteData), .en(WEn5), .clk(Clk), .Q(ReadData5));  // open: clr
  Register #(.width(32)) register_19 (.D(WriteData), .en(WEn13), .clk(Clk), .Q(ReadData13));  // open: clr
  Register #(.width(32)) register_20 (.D(WriteData), .en(WEn21), .clk(Clk), .Q(ReadData21));  // open: clr
  Register #(.width(32)) register_21 (.D(WriteData), .en(WEn29), .clk(Clk), .Q(ReadData29));  // open: clr
  Register #(.width(32)) register_22 (.D(WriteData), .en(WEn6), .clk(Clk), .Q(ReadData6));  // open: clr
  Register #(.width(32)) register_23 (.D(WriteData), .en(WEn14), .clk(Clk), .Q(ReadData14));  // open: clr
  Register #(.width(32)) register_24 (.D(WriteData), .en(WEn22), .clk(Clk), .Q(ReadData22));  // open: clr
  Register #(.width(32)) register_25 (.D(WriteData), .en(WEn30), .clk(Clk), .Q(ReadData30));  // open: clr
  Register #(.width(32)) register_26 (.D(WriteData), .en(WEn7), .clk(Clk), .Q(ReadData7));  // open: clr
  Register #(.width(32)) register_27 (.D(WriteData), .en(WEn15), .clk(Clk), .Q(ReadData15));  // open: clr
  Register #(.width(32)) register_28 (.D(WriteData), .en(WEn23), .clk(Clk), .Q(ReadData23));  // open: clr
  Register #(.width(32)) register_29 (.D(WriteData), .en(WEn31), .clk(Clk), .Q(ReadData31));  // open: clr

  // Other names for the same wires on the sheet: Clock = Clk; WriteToReg[31:0] = WriteData
endmodule

module RegProcess (
  input  [31:0] WriteData,
  input  clk,
  input  WriteEnable,
  input  [4:0] rs1,
  input  [4:0] rs2,
  input  [4:0] rd,
  output [31:0] rs1_Output,
  output [31:0] rs2_Output,
  output [31:0] x0_output,
  output [31:0] ra_output,
  output [31:0] sp_output,
  output [31:0] t0_output,
  output [31:0] t1_output,
  output [31:0] t2_output,
  output [31:0] s0_output,
  output [31:0] s1_output,
  output [31:0] a0_output
);

  wire demultiplexer_1_out0, demultiplexer_1_out1, demultiplexer_1_out2, demultiplexer_1_out3,
       demultiplexer_1_out4, demultiplexer_1_out5, demultiplexer_1_out6, demultiplexer_1_out7,
       demultiplexer_1_out8, demultiplexer_1_out9, demultiplexer_1_out10, demultiplexer_1_out11,
       demultiplexer_1_out12, demultiplexer_1_out13, demultiplexer_1_out14, demultiplexer_1_out15,
       demultiplexer_1_out16, demultiplexer_1_out17, demultiplexer_1_out18, demultiplexer_1_out19,
       demultiplexer_1_out20, demultiplexer_1_out21, demultiplexer_1_out22, demultiplexer_1_out23,
       demultiplexer_1_out24, demultiplexer_1_out25, demultiplexer_1_out26, demultiplexer_1_out27,
       demultiplexer_1_out28, demultiplexer_1_out29, demultiplexer_1_out30, demultiplexer_1_out31;
  wire [31:0] x3, x4, x11, x12, x13, x14, x15, x16, x17, x18, x19, x20, x21, x22, x23, x24, x25, x26, x27,
       x28, x29, x30, x31;

  Demultiplexer #(.enable("false"), .select(5)) demultiplexer_1 (
    .out0(demultiplexer_1_out0), .out1(demultiplexer_1_out1), .out2(demultiplexer_1_out2),
    .out3(demultiplexer_1_out3), .out4(demultiplexer_1_out4), .out5(demultiplexer_1_out5),
    .out6(demultiplexer_1_out6), .out7(demultiplexer_1_out7), .out8(demultiplexer_1_out8),
    .out9(demultiplexer_1_out9), .out10(demultiplexer_1_out10), .out11(demultiplexer_1_out11),
    .out12(demultiplexer_1_out12), .out13(demultiplexer_1_out13), .out14(demultiplexer_1_out14),
    .out15(demultiplexer_1_out15), .out16(demultiplexer_1_out16), .out17(demultiplexer_1_out17),
    .out18(demultiplexer_1_out18), .out19(demultiplexer_1_out19), .out20(demultiplexer_1_out20),
    .out21(demultiplexer_1_out21), .out22(demultiplexer_1_out22), .out23(demultiplexer_1_out23),
    .out24(demultiplexer_1_out24), .out25(demultiplexer_1_out25), .out26(demultiplexer_1_out26),
    .out27(demultiplexer_1_out27), .out28(demultiplexer_1_out28), .out29(demultiplexer_1_out29),
    .out30(demultiplexer_1_out30), .out31(demultiplexer_1_out31), .in(WriteEnable), .sel(rd));
  AllRegs allregs_1 (
    .WriteData(WriteData), .Clk(clk), .WEn0(demultiplexer_1_out0), .WEn1(demultiplexer_1_out1),
    .WEn2(demultiplexer_1_out2), .WEn3(demultiplexer_1_out3), .WEn4(demultiplexer_1_out4),
    .WEn5(demultiplexer_1_out5), .WEn6(demultiplexer_1_out6), .WEn7(demultiplexer_1_out7),
    .WEn8(demultiplexer_1_out8), .WEn9(demultiplexer_1_out9), .WEn10(demultiplexer_1_out10),
    .WEn11(demultiplexer_1_out11), .WEn12(demultiplexer_1_out12), .WEn13(demultiplexer_1_out13),
    .WEn14(demultiplexer_1_out14), .WEn15(demultiplexer_1_out15), .WEn16(demultiplexer_1_out16),
    .WEn17(demultiplexer_1_out17), .WEn18(demultiplexer_1_out18), .WEn19(demultiplexer_1_out19),
    .WEn20(demultiplexer_1_out20), .WEn21(demultiplexer_1_out21), .WEn22(demultiplexer_1_out22),
    .WEn23(demultiplexer_1_out23), .WEn24(demultiplexer_1_out24), .WEn25(demultiplexer_1_out25),
    .WEn26(demultiplexer_1_out26), .WEn27(demultiplexer_1_out27), .WEn28(demultiplexer_1_out28),
    .WEn29(demultiplexer_1_out29), .WEn30(demultiplexer_1_out30), .WEn31(demultiplexer_1_out31),
    .ReadData0(x0_output), .ReadData1(ra_output), .ReadData2(sp_output), .ReadData3(x3), .ReadData4(x4),
    .ReadData5(t0_output), .ReadData6(t1_output), .ReadData7(t2_output), .ReadData8(s0_output),
    .ReadData9(s1_output), .ReadData10(a0_output), .ReadData11(x11), .ReadData12(x12), .ReadData13(x13),
    .ReadData14(x14), .ReadData15(x15), .ReadData16(x16), .ReadData17(x17), .ReadData18(x18),
    .ReadData19(x19), .ReadData20(x20), .ReadData21(x21), .ReadData22(x22), .ReadData23(x23),
    .ReadData24(x24), .ReadData25(x25), .ReadData26(x26), .ReadData27(x27), .ReadData28(x28),
    .ReadData29(x29), .ReadData30(x30), .ReadData31(x31));
  Multiplexer #(.enable("false"), .select(5), .width(32)) multiplexer_1 (
    .in0(x0_output), .in1(ra_output), .in2(sp_output), .in3(x3), .in4(x4), .in5(t0_output), .in6(t1_output),
    .in7(t2_output), .in8(s0_output), .in9(s1_output), .in10(a0_output), .in11(x11), .in12(x12), .in13(x13),
    .in14(x14), .in15(x15), .in16(x16), .in17(x17), .in18(x18), .in19(x19), .in20(x20), .in21(x21),
    .in22(x22), .in23(x23), .in24(x24), .in25(x25), .in26(x26), .in27(x27), .in28(x28), .in29(x29),
    .in30(x30), .in31(x31), .out(rs1_Output), .sel(rs1));
  Multiplexer #(.enable("false"), .select(5), .width(32)) multiplexer_2 (
    .in0(x0_output), .in1(ra_output), .in2(sp_output), .in3(x3), .in4(x4), .in5(t0_output), .in6(t1_output),
    .in7(t2_output), .in8(s0_output), .in9(s1_output), .in10(a0_output), .in11(x11), .in12(x12), .in13(x13),
    .in14(x14), .in15(x15), .in16(x16), .in17(x17), .in18(x18), .in19(x19), .in20(x20), .in21(x21),
    .in22(x22), .in23(x23), .in24(x24), .in25(x25), .in26(x26), .in27(x27), .in28(x28), .in29(x29),
    .in30(x30), .in31(x31), .out(rs2_Output), .sel(rs2));

  // Other names for the same wires on the sheet: x0[31:0] = x0_output; x1[31:0] = ra_output; x2[31:0] = sp_output;
  //   x5[31:0] = t0_output; x6[31:0] = t1_output; x7[31:0] = t2_output; x8[31:0] = s0_output; x9[31:0] = s1_output;
  //   x10[31:0] = a0_output
endmodule
