// Logisim project Test.circ as structural Verilog: 4 circuits, main circuit main
module main (
  output [31:0] out_1,
  output [31:0] out_2
);

  Multiple multiple_1 (.in_1(32'h2), .in_2(32'h80000000), .out_3(out_1), .out_4(out_2));
endmodule

module Extend (
  input  [31:0] in_1,
  output [7:0] EightBits,
  output [63:0] out_3,
  output [7:0] Output24_31
);

  Adder adder_1 (.a(in_1[7:0]), .b(in_1[15:8]), .out(EightBits));  // open: cin, cout
  assign out_3 = {{32{in_1[31]}}, in_1};  // Bit_Extender bit_extender_1

  assign Output24_31 = in_1[31:24];

  // Other names for the same wires on the sheet: Bits16_23[7:0] = in_1[23:16]; Bits24_31[7:0] = in_1[31:24]
endmodule

module Multiple (
  input  [31:0] in_1,
  input  [31:0] in_2,
  output [31:0] out_3,
  output [31:0] out_4
);

  Multiplier #(.mode("twosComplement"), .width(32)) multiplier_1 (
    .a(in_1), .b(in_2), .out(out_3), .cout(out_4));  // open: cin
endmodule

module DeMux (
  output out_1,
  output out_2,
  output out_3,
  output out_4,
  output out_5,
  output out_6,
  output out_7,
  output out_8,
  output out_9
);

  Demultiplexer #(.enable("false"), .select(5)) demultiplexer_1 (
    .out0(out_1), .out3(out_2), .out6(out_3), .out10(out_4), .out16(out_5), .out20(out_6), .out24(out_7),
    .out29(out_8), .out31(out_9), .in(1'b1), .sel(5'b10100));  // open: out1, out2, out4, out5, out7, out8, out9, out11, out12, out13, out14, out15, out17, out18, out19, out21, out22, out23, out25, out26, out27, out28, out30
endmodule
